# Fritzing sketch RobotEdit1 (saved by Fritzing 0.9.2b)
breadboards: 1

parts:
  Part1 = EasyDriver_v44
  Part2 = Arduino Nano (Rev3.0) (ICSP)
  M1 = Stepper Motor - Bipolar
  J1 = Infrared Proximity Sensor
  BAT1 = BC9VPC [package=bc9vpc]
  Part3 = EasyDriver_v44
  M2 = Stepper Motor - Bipolar
  J2 = Infrared Proximity Sensor
  S1 = Round Pushbutton
  M3 = DC Motor
  U1 = 2-Channel 5v Relay Shield [package=relay-2ch5v10a]
  S2 = Tilt Switch [package=THT]
  LED1 = LED - 5mm [color="Green (560nm)" package="5 mm [THT]"]
  R1 = Resistor [tolerance=±5% resistance=220 package=THT]
  Fuse1 = Fuse with Handler [part_number=Htc-15m]

nets:
  GND: Part1.GND, Part2.GND, J1.GND, BAT1.V-, Part3.GND, J2.GND, M3.pin_2, U1.GND, LED1.cathode
  N1: Part1.V+, Part3.V+, S1.leg0, U1.K1-In
  N2: Part1.STEP, Part2.D3
  N3: Part1.DIR, Part2.D2
  N4: Part1.OUT2A, M1.A
  N5: Part1.OUT2B, M1.C
  N6: Part1.OUT1A, M1.B
  N7: Part1.OUT1B, M1.D
  N8: Part2.D4, J1.Vout
  N9: Part2.D5, Part3.STEP
  N10: Part2.D6, Part3.DIR
  N11: Part2.D7, J2.Vout
  N12: Part2.D8, S2.Pin_2
  VCC: Part2.5V, J1.Vcc, J2.Vcc, U1.VCC, R1.Pin_0
  N13: BAT1.V+, Fuse1.Connector1
  N14: Part3.OUT2A, M2.A
  N15: Part3.OUT2B, M2.C
  N16: Part3.OUT1A, M2.B
  N17: Part3.OUT1B, M2.D
  N18: S1.leg1, Fuse1.Connector2
  N19: M3.pin_1, U1.K1-Off
  N20: U1.IN1, S2.Pin_1

notes:
  motore S
  motore D
  motore lama
  sensore inclinazione
  led on/off
  alimentazione motori (anche 12v)
  accensione e fusibile

custom parts:
  2-Channel 5v Relay Shield: 2 Channel 5v Relay Shield w. 2x SPD-06VDC-SD-C

// code stored in the sketch: Robot.ino
/*     Andrea Demetrio Rocca
        Copyleft
       *  Il codice viene fornito cosi come si trova senza alcuna responsabilita dell'utilizzo che ne verra fatto
       *   Per consigli, dubbi o critiche non esitate a contattarci sul canale "GDA - Tutorial per te" o alla mail "gdasteam@gmail.com"!!
*/


#define DIRD 2         //direzione motore destra
#define STEPD 3        //pin di step motore destra
#define IRD 4          //sensore IR a destra
#define DIRS 5         //direzione motore sinistra
#define STEPS 6        //pin di step motore sinistra
#define IRS 7          //sensore IR sinistra
#define LAMA 8         //rele di controllo motore lama
#define INTERVALLO 10  //durata del movimento generale
 
int rilevamentoD = HIGH;
int rilevamentoS = HIGH;

int ritorno = 100;     //durata della rotazione senza controllare nuovamente (variabile perche nel programma il robot potra adattarlo in base alle condizioni)

int i;

void setup()
 {
  Serial.begin(9600);  //inizio della trasmissione seriale (serve soprattutto a noi per capire a che punto del programma si trova)
  Serial.print("Mi sono acceso correttamente.");
  delay(500);

  pinMode(DIRD, OUTPUT);
  pinMode(STEPD, OUTPUT);
  pinMode(IRD, INPUT); 
  pinMode(DIRS, OUTPUT);
  pinMode(STEPS, OUTPUT);
  pinMode(IRS, INPUT);
  pinMode(LAMA, OUTPUT); 
 }
 
void step(boolean dirAttualeD, boolean dirAttualeS, int steps)
{
  digitalWrite(DIRD, dirAttualeD); //invia al driver destro la direzione attuale
  digitalWrite(DIRS, dirAttualeS); //invia al driver sinistro la direzione attuale
  for(int i=0; i<steps; i++)       //ATTENZIONE: durante il ciclo non controlla i sensori!
  {
    digitalWrite(STEPD, HIGH);
    delay(1.2);
    digitalWrite(STEPS, LOW);
    delay(1.2);
    digitalWrite(STEPD, LOW);
    delay(1.2);
    digitalWrite(STEPS, HIGH);
    delay(1.2);
  }
}
 
void loop()
{
  rilevamentoD = digitalRead(IRD); //rileva la condizione del sensore destro
  rilevamentoS = digitalRead(IRS); //rileva la condizione del sensore sinistro
if(rilevamentoD == HIGH && rilevamentoS == HIGH) //se sentrambi non rilevano ostacoli
{
   Serial.print("\nVia libera!");
   step(true, false, INTERVALLO); //ATTENZIONE: i motori sono opposti sullo stesso asse quindi le rotazioni in senso discorde manderanno avanti o indietro il robot!
}
else
{
  if(rilevamentoD == LOW) //se il sensore destro rileva un ostacolo
  {
    Serial.print("\nOstacolo a destra!");
    for(i=0; i<ritorno; i++) //ripeti ritorno-1 volte la funzione senza ricontrollare i sensori
    {
    step(false, false, INTERVALLO); //ATTENZIONE: i motori sono opposti sullo stesso asse quindi le rotazioni in senso concorde faranno ruotare il robot!
    }
 }
 if(rilevamentoS == LOW) //se il sensore sinistro rileva un ostacolo
 {
    Serial.print("\nOstacolo a sinistra!");
    for(i=0; i<ritorno; i++) //ripeti ritorno-1 volte la funzione senza ricontrollare i sensori
    {
    step(true, true, INTERVALLO); //ATTENZIONE: i motori sono opposti sullo stesso asse quindi le rotazioni in senso concorde faranno ruotare il robot!
    }
 }  
}
}
